# Fritzing sketch wired_joystick_L293D (saved by Fritzing 0.9.2b)

parts:
  Part2 = Thumb Joystick
  Part3 = Moteino R4
  U1 = RJ45 Jack [package=rj45-8]
  IC1 = L293D [package=THT]
  J1 = Power Jack [package=power_jack_combo]

nets:
  N1: Part2.GND, Part3.GND-1
  N2: Part2.HORZ, Part3.A0/D14
  N3: Part2.VERT, Part3.A1/D15
  N4: Part2.VCC, Part3.3v3-1
  N5: Part3.D3/INT1, IC1.In_4
  N6: Part3.D4, IC1.In_3
  N7: Part3.D5, IC1.Enable_2
  N8: Part3.D7, IC1.In_1
  N9: Part3.D8, IC1.In_2
  N10: Part3.D9, IC1.Enable_1
  N11: Part3.3v3-2, IC1.+V
  N12: Part3.GND-2, IC1.0V, J1.GND
  N13: U1.5, IC1.Out_4_(_Controlled_by_Enable_2_)
  N14: U1.6, IC1.Out_3_(_Controlled_by_Enable_2_)
  N15: U1.7, IC1.Out_2_(_Controlled_by_Enable_1_)
  N16: U1.8, IC1.Out_1_(_Controlled_by_Enable_1_)
  N17: IC1.+Vmotor, J1.PWR

custom parts:
  Moteino R4: Moteino (revision 4) is a low cost, low power, open source, wireless Arduino UNO development platform clone based on the popular ATMega328 chip used in traditional Arduinos, making it 100% compatible with the Arduino IDE (programming environment). Unlike traditional Arduinos, the Moteino does not include an onboard USB-Serial converter, instead you need to use an external FTDI adapter to load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
