# Fritzing sketch wired_joystick_TB6612FNG (saved by Fritzing 0.9.2b)

parts:
  Part2 = Thumb Joystick
  Part3 = Moteino R4
  U1 = RJ45 Jack [package=rj45-8]
  J1 = Power Jack [package=power_jack_combo]
  Part4 = Motor Driver 1A Dual TB6612FNG

nets:
  N1: Part2.GND, Part3.GND-1
  N2: Part2.HORZ, Part3.A0/D14
  N3: Part2.VERT, Part3.A1/D15
  N4: Part2.VCC, Part3.3v3-1
  N5: Part3.D3/INT1, Part4.PWMA
  N6: Part3.D5, Part4.PWMB
  N7: Part3.D6, Part4.BIN1
  N8: Part3.D7, Part4.BIN2
  N9: Part3.D8, Part4.AIN2
  N10: Part3.D9, Part4.AIN1
  N11: Part3.D10, Part4.STBY
  N12: Part3.3v3-2, Part4.VCC
  GND: Part3.GND-2, J1.GND, J1.GNDBREAK, Part4.GND
  N13: U1.5, Part4.B01
  N14: U1.6, Part4.B02
  N15: U1.7, Part4.A02
  N16: U1.8, Part4.A01
  N17: J1.PWR, Part4.VM

custom parts:
  Moteino R4: Moteino (revision 4) is a low cost, low power, open source, wireless Arduino UNO development platform clone based on the popular ATMega328 chip used in traditional Arduinos, making it 100% compatible with the Arduino IDE (programming environment). Unlike traditional Arduinos, the Moteino does not include an onboard USB-Serial converter, instead you need to use an external FTDI adapter to load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
