# Fritzing sketch wired_joystick_control (saved by Fritzing 0.9.2b)

parts:
  Part1 = Arduino Uno (Rev3)
  DIN1 = DIN-5 jack (MIDI) [package=THT]
  R2 = Rotary Potentiometer (Small) [maximum_resistance=100kΩ package=THT]
  R1 = Rotary Potentiometer (Small) [maximum_resistance=100kΩ package=THT]

nets:
  N1: Part1.A0, R1.wiper
  N2: Part1.A1, R2.wiper
  N3: Part1.D9_PWM, DIN1.3
  N4: Part1.D3_PWM, DIN1.1
  N5: Part1.D5_PWM, DIN1.4
  N6: Part1.D6_PWM, DIN1.5
  N7: Part1.3V3, R2.leg1, R1.leg2
  N8: Part1.GND, R2.leg2, R1.leg1
