# Fritzing sketch wired_switch_control (saved by Fritzing 0.9.2b)
breadboards: 1

parts:
  S1 = Pushbutton [package="[THT]"]
  S2 = Pushbutton [package="[THT]"]
  S3 = Pushbutton [package="[THT]"]
  S4 = Pushbutton [package="[THT]"]
  Part1 = Arduino Uno (Rev3)
  DIN1 = DIN-5 jack (MIDI) [package=THT]

nets:
  N1: S1.Pin_1, S1.Pin_2, Part1.A0
  N2: S1.Pin_3, S1.Pin_4, S2.Pin_3, S2.Pin_4, S3.Pin_3, S3.Pin_4, S4.Pin_3, S4.Pin_4, Part1.GND
  N3: S2.Pin_1, S2.Pin_2, Part1.A1
  N4: S3.Pin_1, S3.Pin_2, Part1.A2
  N5: S4.Pin_1, S4.Pin_2, Part1.A3
  N6: Part1.D8, DIN1.3
  N7: Part1.D3_PWM, DIN1.1
  N8: Part1.D4, DIN1.4
  N9: Part1.D7, DIN1.5
